// Logisim project control-logic.circ as structural Verilog: 1 circuit, main circuit control_logic
module control_logic (
  input  [31:0] Instruction,
  input  BrEq,
  input  BrLt,
  output PCSel,
  output RegWEn,
  output [2:0] ImmSel,
  output BrUn,
  output ASel,
  output BSel,
  output [3:0] ALUSel,
  output MemRW,
  output [1:0] WBSel
);

  wire and_1_out, and_2_out, and_3_out, and_4_out, and_7_out, and_8_out, and_9_out, and_10_out, and_11_out,
       and_12_out, and_13_out, and_14_out, and_15_out, Btype, comparator_4_eq, comparator_5_eq,
       comparator_6_eq, comparator_7_eq, not_2_out, not_3_out, not_4_out, not_5_out, not_6_out, not_7_out,
       not_8_out, or_1_out, or_8_out, or_9_out, RItype, Rtype, Stype;
  wire [2:0] bit_extender_1_out, multiplexer_1_out, not_1_out;

  Comparator #(.width(5)) comparator_1 (.a(Instruction[6:2]), .b(5'b00100), .eq(RItype));  // open: gt, lt
  Comparator #(.width(5)) comparator_2 (.a(Instruction[6:2]), .b(5'b01100), .eq(Rtype));  // open: gt, lt
  Comparator #(.width(5)) comparator_3 (.a(Instruction[6:2]), .b(5'b11000), .eq(Btype));  // open: gt, lt
  Comparator #(.mode("unsigned"), .width(3)) comparator_4 (
    .a(Instruction[14:12]), .b(3'b101), .eq(comparator_4_eq));  // open: gt, lt
  Comparator #(.mode("unsigned"), .width(3)) comparator_5 (
    .a(Instruction[14:12]), .b(3'b000), .eq(comparator_5_eq));  // open: gt, lt
  and and_1 (and_1_out, Instruction[25], Rtype);
  Comparator #(.mode("unsigned"), .width(3)) comparator_6 (
    .a(Instruction[14:12]), .b(3'b101), .eq(comparator_6_eq));  // open: gt, lt
  or or_1 (or_1_out, comparator_4_eq, comparator_5_eq);
  and and_2 (and_2_out, Instruction[30], RItype, comparator_6_eq);
  and and_3 (and_3_out, Instruction[30], Rtype, or_1_out);
  Comparator #(.width(3)) comparator_7 (.a(Instruction[14:12]), .b(3'b000), .eq(comparator_7_eq));  // open: gt, lt
  assign bit_extender_1_out = {{2{Btype}}, Btype};  // Bit_Extender bit_extender_1
  or or_2 (ALUSel[3], and_2_out, and_3_out, and_1_out);
  Multiplexer #(.width(3)) multiplexer_1 (
    .in0(Instruction[14:12]), .in1(3'b100), .out(multiplexer_1_out), .sel(and_4_out));
  and and_4 (and_4_out, comparator_7_eq, Instruction[30]);
  assign not_1_out = ~bit_extender_1_out;  // NOT_Gate not_1, 3 bits wide
  or or_3 (RegWEn, 1'b0, Rtype, RItype);
  or or_4 (ASel, 1'b0, Btype);
  or or_5 (BSel, 1'b0, Btype, RItype);
  assign ALUSel[2:0] = multiplexer_1_out & not_1_out;  // AND_Gate and_5, 3 bits wide
  and and_6 (BrUn, Btype, Instruction[13]);
  or or_6 (WBSel[0], RItype, Rtype, 1'b0);
  or or_7 (WBSel[1], 1'b0, 1'b0);
  Priority_Encoder priority_encoder_1 (
    .in0(RItype), .in1(Stype), .in2(Btype), .out(ImmSel));  // open: in3, in4, in5, in6, in7, en_in, gs, en_out
  not not_2 (not_2_out, Instruction[12]);
  not not_3 (not_3_out, Instruction[14]);
  not not_4 (not_4_out, Instruction[14]);
  not not_5 (not_5_out, BrEq);
  and and_7 (and_7_out, Instruction[12], not_4_out);
  not not_6 (not_6_out, Instruction[12]);
  not not_7 (not_7_out, BrEq);
  not not_8 (not_8_out, BrLt);
  and and_8 (and_8_out, not_2_out, not_3_out);
  and and_9 (and_9_out, not_5_out, and_7_out);
  and and_10 (and_10_out, not_6_out, Instruction[14]);
  or or_8 (or_8_out, not_7_out, not_8_out);
  and and_11 (and_11_out, Instruction[12], Instruction[14]);
  and and_12 (and_12_out, BrEq, and_8_out);
  and and_13 (and_13_out, BrLt, and_10_out);
  and and_14 (and_14_out, or_8_out, and_11_out);
  or or_9 (or_9_out, and_12_out, and_9_out, and_13_out, and_14_out);
  and and_15 (and_15_out, Btype, or_9_out);
  buf or_10 (PCSel, and_15_out);  // OR_Gate

  assign MemRW = 1'b0;

  // Other names for the same wires on the sheet: opcode[4:0] = Instruction[6:2]; func3[2:0] = Instruction[14:12];
  //   func3_1 = Instruction[12]; func3_2 = Instruction[13]; func3_3 = Instruction[14];
  //   func7[6:0] = Instruction[31:25]; func725 = Instruction[25]; func730 = Instruction[30]

  // Notes on the sheet:
  //   INPUTS to your circuit
  //   DON'T CHANGE THE LOCATIONS OF THE INPUTS AND OUTPUTS!
  //   OUTPUT from your circuit
endmodule
